// Logisim project circuito_vetorial.circ as structural Verilog: 9 circuits, main circuit main
module main (
);

  wire adder_1_cout, and_1_out, Branch, CLK, Reset, S_WE, S_WR, Sel_H, V_WR, W_SR1, W_VR1, Zero;
  wire [1:0] ALUOp, DataToReg, multiplexer_3_out, S_RA, S_RB, V_RA, V_RB, V_RD;
  wire [3:0] Imm, Opcode;
  wire [7:0] adder_1_out, MemDadosSeq_s, MemInstrucao_data, multiplexer_1_out, multiplexer_4_out, PC_q,
       S_DRA, S_DRB, S_DRb_t, S_Mov, ula_seq_1_s, V_DRA0, V_DRA1, V_DRA2, V_DRA3, V_DRB0, V_DRB1, V_DRB2,
       V_DRB3;

  Button button_1 (.out(Reset));
  Clock #(.highDuration(2), .lowDuration(2), .phaseOffset(1)) clock_1 (.out(CLK));
  Adder adder_1 (.a(PC_q), .b(8'h1), .out(adder_1_out), .cin(1'b0), .cout(adder_1_cout));
  LED led_1 (.in(adder_1_cout));
  Multiplexer #(.width(8)) multiplexer_1 (.in0(adder_1_out), .in1(S_DRB), .out(multiplexer_1_out), .sel(and_1_out));
  and and_1 (and_1_out, Branch, Zero);
  Multiplexer #(.width(2)) multiplexer_2 (.in0(V_RA), .in1(2'b01), .out(V_RD), .sel(W_VR1));
  Register PC (.D(multiplexer_1_out), .en(1'b1), .clk(CLK), .Q(PC_q), .clr(Reset));
  ROM MemInstrucao (.addr(PC_q), .data(MemInstrucao_data));
  ROM #(.addrWidth(4)) MemControle (.addr(Opcode));  // open: data
  Mov mov_1 (.Imm(Imm), .R1(S_DRA), .SelH(Sel_H), .S(S_Mov));
  Multiplexer #(.width(2)) multiplexer_3 (.in0(S_RA), .in1(2'b01), .out(multiplexer_3_out), .sel(W_SR1));
  Decodificador decodificador_1 (
    .Inst(MemInstrucao_data), .Imm(Imm), .V_RA(V_RA), .S_RA(S_RA), .V_RB(V_RB), .S_RB(S_RB), .Opcode(Opcode));
  BR_seq br_seq_1 (
    .Reset(Reset), .Clk(CLK), .Dados(multiplexer_4_out), .WriteReg(S_WR), .RW(multiplexer_3_out),
    .RA(multiplexer_3_out), .RB(S_RB), .DRA(S_DRA), .DRB(S_DRb_t));
  BR_vet br_vet_1 (
    .Reset(Reset), .Clk(CLK), .VR0({8{1'b0}}), .WriteReg(V_WR), .RW(V_RD), .RA(V_RD), .RB(V_RB),
    .DRA(V_DRA0), .DRB(V_DRB0));  // open: Dados
  BR_vet br_vet_2 (
    .Reset(Reset), .Clk(CLK), .VR0(8'h1), .WriteReg(V_WR), .RW(V_RD), .RA(V_RD), .RB(V_RB), .DRA(V_DRA1),
    .DRB(V_DRB1));  // open: Dados
  BR_vet br_vet_3 (
    .Reset(Reset), .Clk(CLK), .VR0(8'h2), .WriteReg(V_WR), .RW(V_RD), .RA(V_RD), .RB(V_RB), .DRA(V_DRA2),
    .DRB(V_DRB2));  // open: Dados
  BR_vet br_vet_4 (
    .Reset(Reset), .Clk(CLK), .VR0(8'h3), .WriteReg(V_WR), .RW(V_RD), .RA(V_RD), .RB(V_RB), .DRA(V_DRA3),
    .DRB(V_DRB3));  // open: Dados
  ULA_seq ula_seq_1 (.A(S_DRA), .B(S_DRB), .Funct(ALUOp), .Zero(Zero), .S(ula_seq_1_s));
  ULA_vet ula_vet_1 ();  // open: A, B, Funct, S
  ULA_vet ula_vet_2 ();  // open: A, B, Funct, S
  ULA_vet ula_vet_3 ();  // open: A, B, Funct, S
  ULA_vet ula_vet_4 ();  // open: A, B, Funct, S
  MemDados MemDadosSeq (.Addr(S_DRB), .WE(S_WE), .Clk(CLK), .Dados(ula_seq_1_s), .S(MemDadosSeq_s));
  Multiplexer #(.select(2), .width(8)) multiplexer_4 (
    .in0(ula_seq_1_s), .in1(MemDadosSeq_s), .in2(S_Mov), .in3({8{1'b0}}), .out(multiplexer_4_out),
    .sel(DataToReg));
endmodule

module BR_seq (
  input  Reset,
  input  Clk,
  input  [7:0] Dados,
  input  WriteReg,
  input  [1:0] RW,
  input  [1:0] RA,
  input  [1:0] RB,
  output [7:0] DRA,
  output [7:0] DRB
);

  wire demultiplexer_1_out0, demultiplexer_1_out1, demultiplexer_1_out2, demultiplexer_1_out3;
  wire [7:0] SR0_q, SR1_q, SR2_q, SR3_q;

  Demultiplexer #(.select(2)) demultiplexer_1 (
    .out0(demultiplexer_1_out0), .out1(demultiplexer_1_out1), .out2(demultiplexer_1_out2),
    .out3(demultiplexer_1_out3), .in(WriteReg), .sel(RW));
  Register SR0 (.D({8{1'b0}}), .en(demultiplexer_1_out0), .clk(Clk), .Q(SR0_q), .clr(Reset));
  Register SR1 (.D(Dados), .en(demultiplexer_1_out1), .clk(Clk), .Q(SR1_q), .clr(Reset));
  Register SR2 (.D(Dados), .en(demultiplexer_1_out2), .clk(Clk), .Q(SR2_q), .clr(Reset));
  Register SR3 (.D(Dados), .en(demultiplexer_1_out3), .clk(Clk), .Q(SR3_q), .clr(Reset));
  Multiplexer #(.select(2), .width(8)) multiplexer_1 (
    .in0(SR0_q), .in1(SR1_q), .in2(SR2_q), .in3(SR3_q), .out(DRA), .sel(RA));
  // Probe on DRA
  Multiplexer #(.select(2), .width(8)) multiplexer_2 (
    .in0(SR0_q), .in1(SR1_q), .in2(SR2_q), .in3(SR3_q), .out(DRB), .sel(RB));
  // Probe on DRB
endmodule

module BR_vet (
  input  Reset,
  input  Clk,
  input  [7:0] Dados,
  input  [7:0] VR0,
  input  WriteReg,
  input  [1:0] RW,
  input  [1:0] RA,
  input  [1:0] RB,
  output [7:0] DRA,
  output [7:0] DRB
);

  wire demultiplexer_1_out0, demultiplexer_1_out1, demultiplexer_1_out2, demultiplexer_1_out3;
  wire [7:0] VR1_q, VR2_q, VR3_q;

  LED led_1 (.in(demultiplexer_1_out0));
  Demultiplexer #(.select(2)) demultiplexer_1 (
    .out0(demultiplexer_1_out0), .out1(demultiplexer_1_out1), .out2(demultiplexer_1_out2),
    .out3(demultiplexer_1_out3), .in(WriteReg), .sel(RW));
  Register VR1 (.D(Dados), .en(demultiplexer_1_out1), .clk(Clk), .Q(VR1_q), .clr(Reset));
  Register VR2 (.D(Dados), .en(demultiplexer_1_out2), .clk(Clk), .Q(VR2_q), .clr(Reset));
  Register VR3 (.D(Dados), .en(demultiplexer_1_out3), .clk(Clk), .Q(VR3_q), .clr(Reset));
  Multiplexer #(.select(2), .width(8)) multiplexer_1 (
    .in0(VR0), .in1(VR1_q), .in2(VR2_q), .in3(VR3_q), .out(DRA), .sel(RA));
  // Probe on DRA
  Multiplexer #(.select(2), .width(8)) multiplexer_2 (
    .in0(VR0), .in1(VR1_q), .in2(VR2_q), .in3(VR3_q), .out(DRB), .sel(RB));
  // Probe on DRB
endmodule

module ULA_vet (
  input  [7:0] A,
  input  [7:0] B,
  input  Funct,
  output [7:0] S
);

  wire adder_1_cout, subtractor_1_bout;
  wire [7:0] adder_1_out, subtractor_1_out;

  Adder adder_1 (.a(A), .b(B), .out(adder_1_out), .cin(1'b0), .cout(adder_1_cout));
  LED led_1 (.in(adder_1_cout));
  Subtractor subtractor_1 (.a(A), .b(B), .out(subtractor_1_out), .bin(1'b0), .bout(subtractor_1_bout));
  LED led_2 (.in(subtractor_1_bout));
  Multiplexer #(.width(8)) multiplexer_1 (.in0(adder_1_out), .in1(subtractor_1_out), .out(S), .sel(Funct));

  // Notes on the sheet:
  //   A + B
  //   A - B
endmodule

module ULA_seq (
  input  [7:0] A,
  input  [7:0] B,
  input  [1:0] Funct,
  output Zero,
  output [7:0] S
);

  wire adder_1_cout, comparator_1_gt, comparator_1_lt, subtractor_1_bout;
  wire [7:0] D0, D1, D2;

  Comparator comparator_1 (.a(A), .b({8{1'b0}}), .gt(comparator_1_gt), .eq(Zero), .lt(comparator_1_lt));
  Adder adder_1 (.a(A), .b(B), .out(D0), .cin(1'b0), .cout(adder_1_cout));
  Subtractor subtractor_1 (.a(A), .b(B), .out(D1), .bin(1'b0), .bout(subtractor_1_bout));
  assign D2 = A & B;  // AND_Gate and_1, 8 bits wide
  LED led_1 (.in(comparator_1_gt));
  LED led_2 (.in(comparator_1_lt));
  LED led_3 (.in(adder_1_cout));
  LED led_4 (.in(subtractor_1_bout));
  Multiplexer #(.select(2), .width(8)) multiplexer_1 (
    .in0(D0), .in1(D1), .in2(D1), .in3({8{1'b0}}), .out(S), .sel(Funct));

  // Notes on the sheet:
  //   Comparador
  //   A + B
  //   A - B
  //   A and B
endmodule

module Decodificador (
  input  [7:0] Inst,
  output [3:0] Imm,
  output [1:0] V_RA,
  output [1:0] S_RA,
  output [1:0] V_RB,
  output [1:0] S_RB,
  output [3:0] Opcode
);

  Demultiplexer #(.width(2)) demultiplexer_1 (.out0(V_RA), .out1(S_RA), .in(Inst[1:0]), .sel(Inst[7]));
  Demultiplexer #(.width(2)) demultiplexer_2 (.out0(V_RB), .out1(S_RB), .in(Inst[3:2]), .sel(Inst[7]));

  assign Imm = Inst[3:0];
  assign Opcode = Inst[7:4];
endmodule

module ExtensorSinal (
  input  [3:0] A,
  output [7:0] B
);


  assign B = {{5{A[3]}}, A[2:0]};
endmodule

module MemDados (
  input  [7:0] Addr,
  input  WE,
  input  Clk,
  input  [7:0] Dados,
  output [7:0] S
);

  RAM ram_1 (.addr(Addr), .we(WE), .oe(1'b1), .clk(Clk), .din(Dados), .dout(S));
endmodule

module Mov (
  input  [3:0] Imm,
  input  [7:0] R1,
  input  SelH,
  output [7:0] S
);

  Multiplexer #(.width(8)) multiplexer_1 (.in0({R1[7:4], Imm}), .in1({Imm, R1[3:0]}), .out(S), .sel(SelH));

  // Other names for the same wires on the sheet: Mov_H[7:0] = {Imm, R1[3:0]}; R_low[3:0] = R1[3:0];
  //   Mov_L[7:0] = {R1[7:4], Imm}; R_High[3:0] = R1[7:4]
endmodule
